// Logisim project Logisim krets.circ as structural Verilog
module Laboration2 (
  input  q0,
  input  q1,
  input  q2,
  input  q3,
  output y
);
endmodule

module Lab2 (
  input  q0,
  input  q1,
  input  q2,
  input  q3,
  output y
);

  wire and_1_out, and_2_out, and_3_out, and_4_out, and_5_out, and_6_out, and_7_out, and_8_out, and_9_out,
       and_10_out, and_11_out, and_12_out, and_13_out, not_1_out, not_2_out, not_3_out, not_4_out, not_5_out,
       not_6_out, not_7_out, not_8_out, not_9_out, or_1_out, or_2_out, or_3_out;

  not not_1 (not_1_out, q0);
  and and_1 (and_1_out, not_1_out, not_2_out);
  not not_2 (not_2_out, q1);
  not not_3 (not_3_out, q1);
  and and_2 (and_2_out, not_3_out, q2);
  not not_4 (not_4_out, q0);
  not not_5 (not_5_out, q2);
  not not_6 (not_6_out, q1);
  not not_7 (not_7_out, q2);
  not not_8 (not_8_out, q3);
  not not_9 (not_9_out, q3);
  and and_3 (and_3_out, and_1_out, q2);
  and and_4 (and_4_out, and_2_out, q3);
  and and_5 (and_5_out, not_4_out, q1);
  and and_6 (and_6_out, not_5_out, q3);
  and and_7 (and_7_out, q0, not_6_out);
  and and_8 (and_8_out, not_7_out, not_8_out);
  and and_9 (and_9_out, q0, q1);
  and and_10 (and_10_out, q2, not_9_out);
  or or_1 (or_1_out, and_3_out, and_4_out);
  and and_11 (and_11_out, and_5_out, and_6_out);
  and and_12 (and_12_out, and_7_out, and_8_out);
  and and_13 (and_13_out, and_9_out, and_10_out);
  or or_2 (or_2_out, or_1_out, and_11_out);
  or or_3 (or_3_out, and_12_out, and_13_out);
  or or_4 (y, or_2_out, or_3_out);
endmodule

module Labb2 (
  input  q0,
  input  q1,
  input  q2,
  input  q3,
  output YDOB
);

  wire nand_1_out, nand_2_out, nand_3_out, nand_4_out, nand_5_out, nand_6_out, nand_7_out, nand_8_out,
       nand_9_out, nand_10_out, nand_11_out, nand_12_out, nand_13_out, nand_14_out;

  nand nand_1 (nand_1_out, q0, q0);
  nand nand_2 (nand_2_out, q1, q1);
  nand nand_3 (nand_3_out, q1, q1);
  nand nand_4 (nand_4_out, q0, q0);
  nand nand_5 (nand_5_out, q2, q2);
  nand nand_6 (nand_6_out, q1, q1);
  nand nand_7 (nand_7_out, q2, q2);
  nand nand_8 (nand_8_out, q3, q3);
  nand nand_9 (nand_9_out, q3, q3);
  nand nand_10 (nand_10_out, nand_1_out, nand_2_out, q2);
  nand nand_11 (nand_11_out, nand_3_out, q2, q3);
  nand nand_12 (nand_12_out, nand_4_out, q1, nand_5_out, q3);
  nand nand_13 (nand_13_out, q0, nand_6_out, nand_7_out, nand_8_out);
  nand nand_14 (nand_14_out, q0, q1, q2, nand_9_out);
  nand nand_15 (YDOB, nand_10_out, nand_11_out, nand_12_out, nand_13_out, nand_14_out);
endmodule

module Labb (
  input  q0,
  input  q0_2,
  input  q1,
  input  q1_2,
  input  q2,
  input  in_6,
  input  q3,
  input  in_8,
  input  in_9,
  input  in_10,
  output YDOB
);

  wire and_1_out, and_2_out, and_3_out, and_4_out, and_5_out, and_6_out, and_7_out, and_8_out, and_9_out,
       and_10_out, and_11_out, and_12_out, and_13_out, not_4_out, not_5_out, not_6_out, not_7_out, not_8_out,
       not_9_out, not_10_out, not_11_out, not_12_out, not_13_out, not_14_out, not_15_out, or_1_out, or_2_out,
       or_3_out, transistor_1_out, undriven;

  // NOT_Gate not_1 is placed but not wired
  // NOT_Gate not_2 is placed but not wired
  // NOT_Gate not_3 is placed but not wired
  not not_4 (not_4_out, q0);
  and and_1 (and_1_out, not_4_out, not_5_out);
  not not_5 (not_5_out, q1);
  not not_6 (not_6_out, q1);
  and and_2 (and_2_out, not_6_out, q2);
  not not_7 (not_7_out, q0);
  not not_8 (not_8_out, q2);
  not not_9 (not_9_out, q1);
  not not_10 (not_10_out, q2);
  not not_11 (not_11_out, q3);
  not not_12 (not_12_out, q3);
  and and_3 (and_3_out, and_1_out, q2);
  and and_4 (and_4_out, and_2_out, q3);
  and and_5 (and_5_out, not_7_out, q1);
  and and_6 (and_6_out, not_8_out, q3);
  and and_7 (and_7_out, q0, not_9_out);
  and and_8 (and_8_out, not_10_out, not_11_out);
  and and_9 (and_9_out, q0, q1);
  and and_10 (and_10_out, q2, not_12_out);
  or or_1 (or_1_out, and_3_out, and_4_out);
  and and_11 (and_11_out, and_5_out, and_6_out);
  and and_12 (and_12_out, and_7_out, and_8_out);
  and and_13 (and_13_out, and_9_out, and_10_out);
  Transistor transistor_1 (.in(1'b1), .out(transistor_1_out), .gate(in_9));
  Transistor #(.\type ("n")) transistor_2 (.in(undriven), .out(transistor_1_out), .gate(in_9));
  not not_13 (not_13_out, in_10);
  or or_2 (or_2_out, or_1_out, and_11_out);
  or or_3 (or_3_out, and_12_out, and_13_out);
  LED led_1 (.in(transistor_1_out));
  LED led_2 (.in(not_13_out));
  Transistor transistor_3 ();  // open: in, out, gate
  Transistor #(.\type ("n")) transistor_4 ();  // open: in, out, gate
  Transistor #(.\type ("n")) transistor_5 ();  // open: in, out, gate
  Transistor transistor_6 ();  // open: in, out, gate
  or or_4 (YDOB, or_2_out, or_3_out);
  // OR_Gate or_5 is placed but not wired
  // OR_Gate or_6 is placed but not wired
  // OR_Gate or_7 is placed but not wired
  // OR_Gate or_8 is placed but not wired
  not not_14 (not_14_out, q0_2);
  not not_15 (not_15_out, q0_2);
  // AND_Gate and_14 has open pins: in0=not_14_out, out=open
  // AND_Gate and_15 has open pins: in0=not_15_out, out=open
  // AND_Gate and_16 has open pins: in0=q0_2, out=open
  // AND_Gate and_17 has open pins: in0=q0_2, out=open
endmodule
