// Logisim project logisimkrets.circ as structural Verilog
module Labb3 (
  input  in_1,
  input  a,
  input  b
);

  wire and_1_out, and_2_out, and_3_out, and_4_out, and_5_out, and_6_out, not_1_out, not_2_out, not_3_out,
       not_4_out, not_5_out, not_6_out, not_7_out, not_8_out, not_9_out, not_10_out, or_1_out, or_2_out,
       or_3_out, or_4_out, or_5_out, Q1_q, Q1_qn, Q2_q, undriven, undriven_2;

  not not_1 (not_1_out, undriven);
  not not_2 (not_2_out, a);
  not not_3 (not_3_out, b);
  not not_4 (not_4_out, undriven);
  not not_5 (not_5_out, a);
  not not_6 (not_6_out, b);
  not not_7 (not_7_out, undriven_2);
  not not_8 (not_8_out, a);
  not not_9 (not_9_out, a);
  not not_10 (not_10_out, undriven_2);
  and and_1 (and_1_out, not_1_out, a);
  and and_2 (and_2_out, undriven, not_2_out, not_3_out);
  and and_3 (and_3_out, not_4_out, not_5_out, not_6_out);
  and and_4 (and_4_out, undriven_2, a);
  and and_5 (and_5_out, undriven, not_7_out, not_8_out);
  and and_6 (and_6_out, undriven, not_9_out, b);
  or or_1 (or_1_out, and_1_out, and_2_out);
  or or_2 (or_2_out, and_3_out, and_4_out);
  or or_3 (or_3_out, and_5_out, and_6_out);
  or or_4 (or_4_out, not_10_out, or_1_out);
  or or_5 (or_5_out, or_2_out, or_3_out);
  D_Flip_Flop Q1 (.clk(in_1), .D(or_4_out), .Q(Q1_q), .Qn(Q1_qn));  // open: preset, en, reset
  D_Flip_Flop Q2 (.clk(in_1), .D(or_5_out), .Q(Q2_q));  // open: Qn, preset, en, reset
  LED led_1 (.in(Q1_q));
  LED led_2 (.in(Q2_q));
endmodule

module LABB3 (
  input  q1,
  input  q0,
  input  a,
  input  b,
  input  a_2,
  input  b_2,
  input  a_3,
  input  b_3,
  output Q1_2,
  output Q0_2,
  output Q1_3,
  output Q0_3
);

  wire and_1_out, and_2_out, and_3_out, and_4_out, and_5_out, and_6_out, and_7_out, and_8_out, and_9_out,
       and_10_out, and_11_out, and_12_out, and_13_out, and_14_out, and_15_out, and_16_out, and_17_out,
       and_18_out, button_1_out, Clock_out, nand_1_out, nand_2_out, nand_3_out, not_1_out, not_2_out,
       not_3_out, not_4_out, not_5_out, not_6_out, not_7_out, not_8_out, not_9_out, not_10_out, not_11_out,
       not_12_out, not_13_out, not_14_out, not_15_out, not_16_out, not_17_out, not_18_out, not_19_out,
       not_20_out, not_21_out, not_22_out, not_23_out, not_24_out, or_1_out, or_2_out, or_3_out, or_4_out,
       or_5_out, or_6_out, or_7_out, or_8_out, or_9_out, or_10_out, or_12_out, or_14_out, Q0_q, Q1_q, Q1_qn;

  not not_1 (not_1_out, b_3);
  not not_2 (not_2_out, a_3);
  not not_3 (not_3_out, Q0_3);
  not not_4 (not_4_out, Q1_3);
  and and_1 (and_1_out, not_4_out, a_3);
  and and_2 (and_2_out, Q1_3, not_2_out, not_1_out);
  and and_3 (and_3_out, not_4_out, not_2_out, not_1_out);
  and and_4 (and_4_out, Q0_3, a_3);
  and and_5 (and_5_out, Q1_3, not_3_out, not_2_out);
  and and_6 (and_6_out, Q1_3, not_2_out, b_3);
  or or_1 (or_1_out, not_3_out, or_2_out);
  or or_2 (or_2_out, and_1_out, and_2_out);
  or or_3 (or_3_out, and_3_out, and_4_out);
  nand nand_1 (nand_1_out, and_5_out, and_5_out);
  nand nand_2 (nand_2_out, and_6_out, and_6_out);
  nand nand_3 (nand_3_out, nand_1_out, nand_2_out);
  LED led_1 (.in(or_1_out));
  LED led_2 (.in(or_4_out));
  or or_4 (or_4_out, or_3_out, nand_3_out);
  D_Flip_Flop d_ff_1 (.clk(Clock_out), .D(or_1_out), .Q(Q1_3));  // open: Qn, preset, en, reset
  D_Flip_Flop d_ff_2 (.clk(Clock_out), .D(or_4_out), .Q(Q0_3));  // open: Qn, preset, en, reset
  Button Clock (.out(Clock_out));
  not not_5 (not_5_out, Q1_q);
  not not_6 (not_6_out, a_2);
  not not_7 (not_7_out, b_2);
  not not_8 (not_8_out, Q1_q);
  not not_9 (not_9_out, a_2);
  not not_10 (not_10_out, b_2);
  not not_11 (not_11_out, Q0_q);
  not not_12 (not_12_out, a_2);
  not not_13 (not_13_out, a_2);
  not not_14 (not_14_out, Q0_q);
  and and_7 (and_7_out, not_5_out, a_2);
  and and_8 (and_8_out, Q1_q, not_6_out, not_7_out);
  and and_9 (and_9_out, not_8_out, not_9_out, not_10_out);
  and and_10 (and_10_out, Q0_q, a_2);
  and and_11 (and_11_out, Q1_q, not_11_out, not_12_out);
  and and_12 (and_12_out, Q1_q, not_13_out, b_2);
  or or_5 (or_5_out, and_7_out, and_8_out);
  or or_6 (or_6_out, and_9_out, and_10_out);
  or or_7 (or_7_out, and_11_out, and_12_out);
  LED led_3 (.in(or_8_out));
  or or_8 (or_8_out, not_14_out, or_5_out);
  or or_9 (or_9_out, or_6_out, or_7_out);
  LED led_4 (.in(or_9_out));
  not not_15 (not_15_out, q1);
  not not_16 (not_16_out, a);
  not not_17 (not_17_out, b);
  not not_18 (not_18_out, q1);
  not not_19 (not_19_out, a);
  not not_20 (not_20_out, b);
  not not_21 (not_21_out, q0);
  not not_22 (not_22_out, a);
  not not_23 (not_23_out, a);
  D_Flip_Flop u_Q1 (.clk(button_1_out), .D(or_8_out), .Q(Q1_q), .Qn(Q1_qn));  // open: preset, en, reset
  LED led_5 (.in(Q1_q));
  LED led_6 (.in(Q0_q));
  D_Flip_Flop u_Q0 (.clk(button_1_out), .D(or_9_out), .Q(Q0_q));  // open: Qn, preset, en, reset
  not not_24 (not_24_out, q0);
  and and_13 (and_13_out, not_15_out, a);
  or or_10 (or_10_out, and_13_out, and_14_out);
  and and_14 (and_14_out, q1, not_16_out, not_17_out);
  and and_15 (and_15_out, not_18_out, not_19_out, not_20_out);
  and and_16 (and_16_out, q0, a);
  and and_17 (and_17_out, q1, not_21_out, not_22_out);
  and and_18 (and_18_out, q1, not_23_out, b);
  Button button_1 (.out(button_1_out));
  or or_11 (Q1_2, not_24_out, or_10_out);
  or or_12 (or_12_out, and_15_out, and_16_out);
  or or_13 (Q0_2, or_12_out, or_14_out);
  or or_14 (or_14_out, and_17_out, and_18_out);
endmodule

module lol (
  input  q1,
  input  q1_2,
  input  q0,
  input  q0_2,
  input  a,
  input  a_2,
  input  b,
  input  b_2,
  input  a_3,
  input  b_3,
  input  a_4,
  input  b_4,
  output Q1_3,
  output Q1_4,
  output Q0_3,
  output Q0_4,
  output Q1_5,
  output Q0_5
);

  wire and_1_out, and_2_out, and_3_out, and_4_out, and_5_out, and_6_out, and_7_out, and_8_out, and_9_out,
       and_10_out, and_11_out, and_12_out, and_13_out, and_14_out, and_15_out, and_16_out, and_17_out,
       and_18_out, and_19_out, and_20_out, and_21_out, and_22_out, and_23_out, and_24_out, button_1_out,
       Clock_out, nand_1_out, nand_2_out, nand_3_out, nand_4_out, nand_5_out, nand_6_out, not_1_out,
       not_2_out, not_3_out, not_4_out, not_5_out, not_6_out, not_7_out, not_8_out, not_9_out, not_10_out,
       not_11_out, not_12_out, not_13_out, not_14_out, not_15_out, not_16_out, not_17_out, not_18_out,
       not_19_out, not_20_out, not_21_out, not_22_out, not_23_out, not_24_out, not_25_out, not_26_out,
       not_27_out, not_28_out, not_29_out, not_30_out, not_31_out, not_32_out, not_33_out, not_34_out,
       or_3_out, or_4_out, or_5_out, or_6_out, or_7_out, or_9_out, or_11_out, or_12_out, or_13_out,
       or_14_out, or_15_out, Q0_q, Q1_q, Q1_qn;

  not not_1 (not_1_out, b_4);
  not not_2 (not_2_out, q0);
  not not_3 (not_3_out, q1);
  and and_1 (and_1_out, not_3_out, a);
  not not_4 (not_4_out, a);
  and and_2 (and_2_out, q1, not_4_out, not_5_out);
  not not_5 (not_5_out, b);
  not not_6 (not_6_out, q1);
  not not_7 (not_7_out, a);
  and and_3 (and_3_out, not_6_out, not_7_out, not_8_out);
  not not_8 (not_8_out, b);
  and and_4 (and_4_out, q0, a);
  not not_9 (not_9_out, q0);
  and and_5 (and_5_out, q1, not_9_out, not_10_out);
  not not_10 (not_10_out, a);
  and and_6 (and_6_out, q1, not_11_out, b);
  not not_11 (not_11_out, a);
  not not_12 (not_12_out, a_4);
  or or_1 (Q1_4, not_2_out, and_1_out, and_2_out);
  or or_2 (Q0_3, and_3_out, and_4_out, and_5_out, and_6_out);
  not not_13 (not_13_out, Q0_5);
  not not_14 (not_14_out, Q1_5);
  not not_15 (not_15_out, q1_2);
  not not_16 (not_16_out, a_2);
  not not_17 (not_17_out, b_2);
  not not_18 (not_18_out, q1_2);
  not not_19 (not_19_out, a_2);
  not not_20 (not_20_out, b_2);
  not not_21 (not_21_out, q0_2);
  not not_22 (not_22_out, a_2);
  not not_23 (not_23_out, a_2);
  and and_7 (and_7_out, not_14_out, a_4);
  and and_8 (and_8_out, Q1_5, not_12_out, not_1_out);
  and and_9 (and_9_out, not_14_out, not_12_out, not_1_out);
  and and_10 (and_10_out, Q0_5, a_4);
  and and_11 (and_11_out, Q1_5, not_13_out, not_12_out);
  and and_12 (and_12_out, Q1_5, not_12_out, b_4);
  not not_24 (not_24_out, q0_2);
  and and_13 (and_13_out, not_15_out, a_2);
  and and_14 (and_14_out, q1_2, not_16_out, not_17_out);
  and and_15 (and_15_out, not_18_out, not_19_out, not_20_out);
  and and_16 (and_16_out, q0_2, a_2);
  and and_17 (and_17_out, q1_2, not_21_out, not_22_out);
  and and_18 (and_18_out, q1_2, not_23_out, b_2);
  or or_3 (or_3_out, not_13_out, or_4_out);
  or or_4 (or_4_out, and_7_out, and_8_out);
  or or_5 (or_5_out, and_9_out, and_10_out);
  nand nand_1 (nand_1_out, and_11_out, and_11_out);
  nand nand_2 (nand_2_out, and_12_out, and_12_out);
  or or_6 (or_6_out, and_13_out, and_14_out);
  or or_7 (or_7_out, and_15_out, and_16_out);
  nand nand_3 (nand_3_out, and_17_out, and_17_out);
  nand nand_4 (nand_4_out, and_18_out, and_18_out);
  nand nand_5 (nand_5_out, nand_1_out, nand_2_out);
  or or_8 (Q1_3, not_24_out, or_6_out);
  nand nand_6 (nand_6_out, nand_3_out, nand_4_out);
  LED led_1 (.in(or_3_out));
  LED led_2 (.in(or_9_out));
  or or_9 (or_9_out, or_5_out, nand_5_out);
  or or_10 (Q0_4, or_7_out, nand_6_out);
  D_Flip_Flop d_ff_1 (.clk(Clock_out), .D(or_3_out), .Q(Q1_5));  // open: Qn, preset, en, reset
  D_Flip_Flop d_ff_2 (.clk(Clock_out), .D(or_9_out), .Q(Q0_5));  // open: Qn, preset, en, reset
  Button Clock (.out(Clock_out));
  not not_25 (not_25_out, Q1_q);
  not not_26 (not_26_out, a_3);
  not not_27 (not_27_out, b_3);
  not not_28 (not_28_out, Q1_q);
  not not_29 (not_29_out, a_3);
  not not_30 (not_30_out, b_3);
  not not_31 (not_31_out, Q0_q);
  not not_32 (not_32_out, a_3);
  not not_33 (not_33_out, a_3);
  not not_34 (not_34_out, Q0_q);
  and and_19 (and_19_out, not_25_out, a_3);
  and and_20 (and_20_out, Q1_q, not_26_out, not_27_out);
  and and_21 (and_21_out, not_28_out, not_29_out, not_30_out);
  and and_22 (and_22_out, Q0_q, a_3);
  and and_23 (and_23_out, Q1_q, not_31_out, not_32_out);
  and and_24 (and_24_out, Q1_q, not_33_out, b_3);
  or or_11 (or_11_out, and_19_out, and_20_out);
  or or_12 (or_12_out, and_21_out, and_22_out);
  or or_13 (or_13_out, and_23_out, and_24_out);
  LED led_3 (.in(or_14_out));
  or or_14 (or_14_out, not_34_out, or_11_out);
  or or_15 (or_15_out, or_12_out, or_13_out);
  LED led_4 (.in(or_15_out));
  D_Flip_Flop u_Q1 (.clk(button_1_out), .D(or_14_out), .Q(Q1_q), .Qn(Q1_qn));  // open: preset, en, reset
  LED led_5 (.in(Q1_q));
  LED led_6 (.in(Q0_q));
  D_Flip_Flop u_Q0 (.clk(button_1_out), .D(or_15_out), .Q(Q0_q));  // open: Qn, preset, en, reset
  Button button_1 (.out(button_1_out));
endmodule
